// Logisim project Task 2.2.circ as structural Verilog: 1 circuit, main circuit main
module main (
  input  D0,
  input  in_2,
  input  D1,
  input  [1:0] in_4,
  input  D2,
  input  D3,
  output Equal
);

  wire multiplexer_1_out, multiplexer_2_out, multiplexer_3_out, multiplexer_4_out;

  Multiplexer #(.select(2)) multiplexer_1 (
    .in0(D0), .in1(D1), .in2(D2), .in3(D3), .out(multiplexer_1_out), .sel(in_4), .en(in_2));
  Multiplexer #(.enable("false")) multiplexer_2 (.in0(D0), .in1(D1), .out(multiplexer_2_out), .sel(in_4[0]));
  Multiplexer #(.enable("false")) multiplexer_3 (.in0(D2), .in1(D3), .out(multiplexer_3_out), .sel(in_4[0]));
  Multiplexer #(.enable("false")) multiplexer_4 (
    .in0(multiplexer_2_out), .in1(multiplexer_3_out), .out(multiplexer_4_out), .sel(in_4[1]));
  xor xor_1 (Equal, multiplexer_1_out, multiplexer_4_out);
endmodule
