// Logisim project Task 5.1.circ as structural Verilog: 2 circuits, main circuit main
module main (
  input  CLK,
  input  D,
  output Q,
  output Q_prime
);

  wire and_1_out, and_2_out, not_1_out;

  and and_1 (and_1_out, CLK, not_1_out);
  not not_1 (not_1_out, D);
  and and_2 (and_2_out, CLK, D);
  nor nor_1 (Q, and_1_out, Q_prime);
  nor nor_2 (Q_prime, Q, and_2_out);
endmodule

module D_FlipFlop (
  input  Din,
  output Qout,
  output out_3,
  output Q_prime_out
);

  wire CLK_out, master_q, not_1_out;

  not not_1 (not_1_out, CLK_out);
  main master (.CLK(Din), .D(not_1_out), .Q(master_q), .Q_prime(out_3));
  Clock CLK (.out(CLK_out));
  main slave (.CLK(master_q), .D(CLK_out), .Q(Qout), .Q_prime(Q_prime_out));
endmodule
