// Logisim project Task 5.2.circ as structural Verilog: 3 circuits, main circuit main
module main (
  input  CLK,
  input  D,
  output Q,
  output Q_prime
);

  wire and_1_out, and_2_out, not_1_out;

  and and_1 (and_1_out, CLK, not_1_out);
  not not_1 (not_1_out, D);
  and and_2 (and_2_out, CLK, D);
  nor nor_1 (Q, and_1_out, Q_prime);
  nor nor_2 (Q_prime, Q, and_2_out);
endmodule

module D_FlipFlop (
  input  Din,
  input  CLK,
  output Qout,
  output Q_prime_out
);

  wire master_q, not_1_out;

  not not_1 (not_1_out, CLK);
  main master (.CLK(Din), .D(not_1_out), .Q(master_q));  // open: Q_prime
  main slave (.CLK(master_q), .D(CLK), .Q(Qout), .Q_prime(Q_prime_out));
endmodule

module _4_bit_register (
  input  [3:0] X,
  output [3:0] Y
);

  wire CLK_out;

  D_FlipFlop d_flipflop_1 (.Din(X[0]), .CLK(CLK_out), .Qout(Y[0]));  // open: Q_prime_out
  D_FlipFlop d_flipflop_2 (.Din(X[1]), .CLK(CLK_out), .Qout(Y[1]));  // open: Q_prime_out
  D_FlipFlop d_flipflop_3 (.Din(X[2]), .CLK(CLK_out), .Qout(Y[2]));  // open: Q_prime_out
  D_FlipFlop d_flipflop_4 (.Din(X[3]), .CLK(CLK_out), .Qout(Y[3]));  // open: Q_prime_out
  Clock CLK (.out(CLK_out));
endmodule
